// Logisim project LAB_04.circ as structural Verilog: 5 circuits, main circuit main
module main (
  input  A,
  input  B,
  input  C,
  input  D,
  input  E,
  input  F,
  output F1,
  output F2,
  output F3
);

  xor xor_1 (F1, A, B);
  xnor xnor_1 (F2, C, D);
  nor nor_1 (F3, E, F);
endmodule

module BCD2GRAY (
  input  B3,
  input  B2,
  input  B1,
  input  B0,
  output D3,
  output D2,
  output D1,
  output D0
);

  wire nand_1_out, nand_2_out, nand_3_out, nand_4_out, nand_5_out, nand_6_out, nand_8_out, nand_9_out,
       nand_10_out, nand_11_out;

  nand nand_1 (nand_1_out, B2, B2);
  nand nand_2 (nand_2_out, B3, B3);
  nand nand_3 (nand_3_out, B2, B2);
  nand nand_4 (nand_4_out, B1, B1);
  nand nand_5 (nand_5_out, B1, B1);
  nand nand_6 (nand_6_out, B0, B0);
  nand nand_7 (D2, nand_1_out, nand_2_out);
  nand nand_8 (nand_8_out, nand_3_out, B1);
  nand nand_9 (nand_9_out, B2, nand_4_out);
  nand nand_10 (nand_10_out, nand_5_out, B0);
  nand nand_11 (nand_11_out, B1, nand_6_out);
  nand nand_12 (D1, nand_8_out, nand_9_out);
  nand nand_13 (D0, nand_10_out, nand_11_out);

  assign D3 = B3;
endmodule

module GRAY2BCD (
  input  D3,
  input  D2,
  input  D1,
  input  D0,
  output B3,
  output B2,
  output B1,
  output B0
);

  xor xor_1 (B2, D3, D2);
  xor xor_2 (B1, B2, D1);
  xor xor_3 (B0, B1, D0);

  assign B3 = D3;
endmodule

module BCD2XS3 (
  input  [3:0] in_1,
  output [3:0] out_2
);

  Adder #(.width(4)) adder_1 (.a(in_1), .b(4'b0011), .out(out_2));  // open: cin, cout
endmodule

module B2X (
  input  B3,
  input  B2,
  input  B1,
  input  B0,
  output X3,
  output X2,
  output X1,
  output X0
);

  wire and_1_out, and_2_out, and_3_out, and_4_out, and_5_out, nor_1_out, not_1_out, not_2_out, not_3_out,
       or_1_out, or_2_out;

  or or_1 (or_1_out, B1, B0);
  not not_1 (not_1_out, B2);
  or or_2 (or_2_out, B1, B0);
  nor nor_1 (nor_1_out, B1, B0);
  and and_1 (and_1_out, B1, B0);
  not not_2 (not_2_out, B1);
  and and_2 (and_2_out, not_2_out, not_3_out);
  not not_3 (not_3_out, B0);
  not not_4 (X0, B0);
  or or_3 (X3, B3, and_3_out);
  and and_3 (and_3_out, B2, or_1_out);
  and and_4 (and_4_out, not_1_out, or_2_out);
  and and_5 (and_5_out, B2, nor_1_out);
  or or_4 (X1, and_1_out, and_2_out);
  or or_5 (X2, and_4_out, and_5_out);
endmodule
